// Logisim project BasketballScoreboard.circ as structural Verilog: 6 circuits, main circuit main
module main (
  input  in_1
);

  wire ADD, ADD1, bcd_to_7_segment_decoder_3_p1, bcd_to_7_segment_decoder_14_p1,
       bcd_to_7_segment_decoder_15_p1, binary_to_bcd_converter_1_p2, binary_to_bcd_converter_1_p4,
       binary_to_bcd_converter_2_p2, binary_to_bcd_converter_4_p2, binary_to_bcd_converter_8_p2, BONUS1,
       BONUS2, CLOCK_1, clock_1_out, clock_2_out, clock_3_out, comparator_2_eq, comparator_3_eq,
       comparator_4_eq, comparator_5_eq, MINUS, MINUS1, n7_segment_display_5_p1, n7_segment_display_6_p1,
       n7_segment_display_7_p1, n7_segment_display_9_p1, n7_segment_display_10_p1, n7_segment_display_11_p1,
       n7_segment_display_12_p1, not_1_out, not_2_out, not_3_out, ONE, ONE1, or_1_out, P, plus123_1_1_f2,
       plus123_1_2_f2, POSS_CHANGE, QUARTER_END, RESET_ATTACK, RESET_TIME, RST, RST1, THREE, THREE1, TWO,
       TWO1;
  wire [1:0] plus123_1_1_f1, plus123_1_2_f1;
  wire [3:0] adder_1_out, adder_2_out, FOULS_AWAY, FOULS_HOME, PERIOD;
  wire [4:0] ATTACK_TIME;
  wire [5:0] MINUTES, SECONDS;
  wire [7:0] adder_3_out, adder_4_out, multiplexer_1_out, multiplexer_2_out, negator_1_out, negator_2_out,
       SCORE_AWAY, SCORE_HOME;

  not not_1 (not_1_out, comparator_3_eq);
  or or_1 (or_1_out, RESET_TIME, RESET_ATTACK);
  not not_2 (not_2_out, comparator_4_eq);
  Counter #(.max('h18), .width(5)) u_ATTACK_TIME (
    .clr(or_1_out), .up(in_1), .clk(CLOCK_1), .D(5'b11000), .Q(ATTACK_TIME));  // open: load, count, carry
  Counter #(.max('h3b), .width(6)) u_SECONDS (
    .clr(RESET_TIME), .load(comparator_3_eq), .up(1'b0), .clk(CLOCK_1), .D(6'b111011), .Q(SECONDS));  // open: count, carry
  Counter #(.max('h9), .width(6)) u_MINUTES (
    .clr(RESET_TIME), .load(comparator_4_eq), .up(1'b0), .clk(not_1_out), .D(6'b001001), .Q(MINUTES));  // open: count, carry
  Counter #(.max('h4), .width(4)) u_PERIOD (
    .clr(RESET_TIME), .load(comparator_5_eq), .clk(not_2_out), .D(4'b0001), .Q(PERIOD));  // open: up, count, carry
  T_Flip_Flop t_ff_1 (.T(1'b1), .clk(POSS_CHANGE), .Qn(P));  // open: Q, reset, preset
  Comparator #(.width(5)) comparator_1 (.a({5{1'b0}}), .b(ATTACK_TIME), .eq(POSS_CHANGE));  // open: gt, lt
  Comparator #(.width(5)) comparator_2 (.a(5'b00001), .b(ATTACK_TIME), .eq(comparator_2_eq));  // open: gt, lt
  and and_1 (QUARTER_END, comparator_3_eq, comparator_4_eq);
  Comparator #(.width(6)) comparator_3 (.a(SECONDS), .b({6{1'b0}}), .eq(comparator_3_eq));  // open: gt, lt
  Comparator #(.width(6)) comparator_4 (.a(MINUTES), .b({6{1'b0}}), .eq(comparator_4_eq));  // open: gt, lt
  Comparator #(.width(4)) comparator_5 (.a(PERIOD), .b(4'b0000), .eq(comparator_5_eq));  // open: gt, lt
  // Buzzer buzzer_1: pin names not known; wires that end beside it: 14'h215, comparator_2_eq, 7'b0110010
  LED led_1 (.in(comparator_2_eq));
  // Buzzer buzzer_2: pin names not known; wires that end beside it: 14'h215, QUARTER_END, 7'b0110010
  _7_Segment_Display u_7_segment_display_1 ();  // open: g, f, a, b, e, d, c, dp
  // BCD_to_7_Segment_decoder bcd_to_7_segment_decoder_1: pin names not known
  // Binary_to_BCD_converter #(.binvalue(8)) binary_to_bcd_converter_1: pin names not known; wires that end beside it: SCORE_HOME, binary_to_bcd_converter_1_p2, binary_to_bcd_converter_1_p2, binary_to_bcd_converter_1_p4
  Button button_1 (.out(ADD));
  _7_Segment_Display u_7_segment_display_2 ();  // open: g, f, a, b, e, d, c, dp
  // BCD_to_7_Segment_decoder bcd_to_7_segment_decoder_2: pin names not known; wires that end beside it: binary_to_bcd_converter_1_p4
  LED led_2 (.in(BONUS1));
  // Binary_to_BCD_converter #(.binvalue(4)) binary_to_bcd_converter_2: pin names not known; wires that end beside it: FOULS_HOME, binary_to_bcd_converter_2_p2
  Button button_2 (.out(ONE));
  Button button_3 (.out(TWO));
  Button button_4 (.out(THREE));
  Button button_5 (.out(MINUS));
  Button button_6 (.out(RST));
  LED led_3 (.in(P));
  _7_Segment_Display u_7_segment_display_3 ();  // open: g, f, a, b, e, d, c, dp
  // BCD_to_7_Segment_decoder bcd_to_7_segment_decoder_3: pin names not known; wires that end beside it: bcd_to_7_segment_decoder_3_p1, bcd_to_7_segment_decoder_3_p1
  _7_Segment_Display u_7_segment_display_4 ();  // open: g, f, a, b, e, d, c, dp
  // BCD_to_7_Segment_decoder bcd_to_7_segment_decoder_4: pin names not known; wires that end beside it: binary_to_bcd_converter_2_p2
  // _7_Segment_Display 7_segment_display_5: pin names not known; wires that end beside it: n7_segment_display_5_p1, n7_segment_display_5_p1
  // _7_Segment_Display 7_segment_display_6: pin names not known; wires that end beside it: n7_segment_display_6_p1, n7_segment_display_6_p1
  // BCD_to_7_Segment_decoder bcd_to_7_segment_decoder_5: pin names not known
  // BCD_to_7_Segment_decoder bcd_to_7_segment_decoder_6: pin names not known
  // Binary_to_BCD_converter #(.binvalue(6)) binary_to_bcd_converter_3: pin names not known; wires that end beside it: MINUTES
  // Binary_to_BCD_converter #(.binvalue(4)) binary_to_bcd_converter_4: pin names not known; wires that end beside it: PERIOD, binary_to_bcd_converter_4_p2
  Clock u_clock_1 (.out(clock_1_out));
  // Switch switch_1: pin names not known; wires that end beside it: clock_1_out, CLOCK_1
  Button RESET_TIMERS (.out(RESET_TIME));
  Button u_RESET_ATTACK (.out(RESET_ATTACK));
  LED led_4 (.in(QUARTER_END));
  // _7_Segment_Display 7_segment_display_7: pin names not known; wires that end beside it: n7_segment_display_7_p1, n7_segment_display_7_p1
  // BCD_to_7_Segment_decoder bcd_to_7_segment_decoder_7: pin names not known
  // Binary_to_BCD_converter #(.binvalue(5)) binary_to_bcd_converter_5: pin names not known; wires that end beside it: ATTACK_TIME
  _7_Segment_Display u_7_segment_display_8 ();  // open: g, f, a, b, e, d, c, dp
  // BCD_to_7_Segment_decoder bcd_to_7_segment_decoder_8: pin names not known; wires that end beside it: binary_to_bcd_converter_4_p2
  // _7_Segment_Display 7_segment_display_9: pin names not known; wires that end beside it: n7_segment_display_9_p1, n7_segment_display_9_p1
  // BCD_to_7_Segment_decoder bcd_to_7_segment_decoder_9: pin names not known
  // _7_Segment_Display 7_segment_display_10: pin names not known; wires that end beside it: n7_segment_display_10_p1, n7_segment_display_10_p1
  // BCD_to_7_Segment_decoder bcd_to_7_segment_decoder_10: pin names not known
  // Binary_to_BCD_converter #(.binvalue(6)) binary_to_bcd_converter_6: pin names not known; wires that end beside it: SECONDS
  not not_3 (not_3_out, P);
  // _7_Segment_Display 7_segment_display_11: pin names not known; wires that end beside it: n7_segment_display_11_p1, n7_segment_display_11_p1
  // BCD_to_7_Segment_decoder bcd_to_7_segment_decoder_11: pin names not known
  // Binary_to_BCD_converter #(.binvalue(4)) binary_to_bcd_converter_7: pin names not known; wires that end beside it: FOULS_AWAY
  LED led_5 (.in(not_3_out));
  // _7_Segment_Display 7_segment_display_12: pin names not known; wires that end beside it: n7_segment_display_12_p1, n7_segment_display_12_p1
  // BCD_to_7_Segment_decoder bcd_to_7_segment_decoder_12: pin names not known
  Button button_7 (.out(TWO1));
  Button button_8 (.out(THREE1));
  Button button_9 (.out(MINUS1));
  Button button_10 (.out(RST1));
  _7_Segment_Display u_7_segment_display_13 ();  // open: g, f, a, b, e, d, c, dp
  _7_Segment_Display u_7_segment_display_14 ();  // open: g, f, a, b, e, d, c, dp
  // BCD_to_7_Segment_decoder bcd_to_7_segment_decoder_13: pin names not known
  // BCD_to_7_Segment_decoder bcd_to_7_segment_decoder_14: pin names not known; wires that end beside it: bcd_to_7_segment_decoder_14_p1
  // Binary_to_BCD_converter #(.binvalue(8)) binary_to_bcd_converter_8: pin names not known; wires that end beside it: SCORE_AWAY, binary_to_bcd_converter_8_p2, binary_to_bcd_converter_8_p2, bcd_to_7_segment_decoder_14_p1
  LED led_6 (.in(BONUS2));
  Button button_11 (.out(ONE1));
  _7_Segment_Display u_7_segment_display_15 ();  // open: g, f, a, b, e, d, c, dp
  // BCD_to_7_Segment_decoder bcd_to_7_segment_decoder_15: pin names not known; wires that end beside it: bcd_to_7_segment_decoder_15_p1, bcd_to_7_segment_decoder_15_p1
  Button button_12 (.out(ADD1));
  Counter #(.max('h5), .width(4)) u_FOULS_HOME (
    .clr(QUARTER_END), .load(1'b1), .up(1'b1), .clk(ADD), .D(adder_1_out), .Q(FOULS_HOME));  // open: count, carry
  Counter #(.max('h5), .width(4)) FOULS_GUEST (
    .clr(QUARTER_END), .load(1'b1), .up(1'b1), .clk(ADD1), .D(adder_2_out), .Q(FOULS_AWAY));  // open: count, carry
  Adder #(.width(4)) adder_1 (.a(FOULS_HOME), .b(4'b0001), .out(adder_1_out));  // open: cin, cout
  Adder #(.width(4)) adder_2 (.a(FOULS_AWAY), .b(4'b0001), .out(adder_2_out));  // open: cin, cout
  Clock clock_2 (.out(clock_2_out));
  Negator negator_1 (.in(8'h1), .out(negator_1_out));
  Multiplexer #(.enable("true"), .select(2), .width(8)) multiplexer_1 (
    .in0(8'h1), .in1(8'h2), .in2(8'h3), .in3(negator_1_out), .out(multiplexer_1_out), .sel(plus123_1_1_f1),
    .en(plus123_1_1_f2));
  Comparator #(.width(4)) comparator_6 (.a(FOULS_HOME), .b(4'b0101), .eq(BONUS1));  // open: gt, lt
  Comparator #(.width(4)) comparator_7 (.a(FOULS_AWAY), .b(4'b0101), .eq(BONUS2));  // open: gt, lt
  Counter u_SCORE_HOME (
    .clr(RST), .load(1'b1), .up(1'b1), .clk(clock_2_out), .D(adder_3_out), .Q(SCORE_HOME));  // open: count, carry
  PLUS123_1 plus123_1_1 (.A(ONE), .B(TWO), .C(THREE), .D(MINUS), .F1(plus123_1_1_f1), .F2(plus123_1_1_f2));
  Adder adder_3 (.a(SCORE_HOME), .b(multiplexer_1_out), .out(adder_3_out));  // open: cin, cout
  Clock clock_3 (.out(clock_3_out));
  Negator negator_2 (.in(8'h1), .out(negator_2_out));
  Multiplexer #(.enable("true"), .select(2), .width(8)) multiplexer_2 (
    .in0(8'h1), .in1(8'h2), .in2(8'h3), .in3(negator_2_out), .out(multiplexer_2_out), .sel(plus123_1_2_f1),
    .en(plus123_1_2_f2));
  Counter SCORE_GUEST (
    .clr(RST1), .load(1'b1), .up(1'b1), .clk(clock_3_out), .D(adder_4_out), .Q(SCORE_AWAY));  // open: count, carry
  PLUS123_1 plus123_1_2 (.A(ONE1), .B(TWO1), .C(THREE1), .D(MINUS1), .F1(plus123_1_2_f1), .F2(plus123_1_2_f2));
  Adder adder_4 (.a(SCORE_AWAY), .b(multiplexer_2_out), .out(adder_4_out));  // open: cin, cout

  // Notes on the sheet:
  //   ADD FOUL
  //   POINTS
  //   ADD ONE POINT
  //   ADD TWO POINTS
  //   ADD THREE POINTS
  //   DEDUCT ONE POINT
  //   RESET SCORE
  //   BONUS
  //   HOME TEAM
  //   POSSESION
  //   HOME
  //   FOULS
  //   ATTACK TIMER
  //   PERIOD
  //   CONTROLS
  //   STOP/START THE TIME
  //   FOULS
  //   GUEST
  //   BONUS
  //   ADD FOUL
  //   POSSESION
  //   GUEST TEAM
  //   POINTS
  //   ADD ONE POINT
  //   ADD TWO POINTS
  //   ADD THREE POINTS
  //   DEDUCT ONE POINT
  //   RESET SCORE
endmodule

module TIMER (
);

  wire and_1_out, binary_to_bcd_converter_3_p2, clock_1_out, comparator_1_eq, comparator_2_eq,
       comparator_3_eq, n7_segment_display_1_p1, n7_segment_display_2_p1, n7_segment_display_3_p1,
       n7_segment_display_4_p1, n7_segment_display_5_p1, not_1_out, not_2_out, RESET_out;
  wire [3:0] PERIOD_q;
  wire [5:0] MINUTES_q, SECONDS_q;

  Button RESET (.out(RESET_out));
  Clock clock_1 (.out(clock_1_out));
  not not_1 (not_1_out, comparator_1_eq);
  not not_2 (not_2_out, comparator_2_eq);
  Counter #(.max('h3b), .width(6)) SECONDS (
    .clr(RESET_out), .load(comparator_1_eq), .up(1'b0), .clk(clock_1_out), .D(6'b111011), .Q(SECONDS_q));  // open: count, carry
  Counter #(.max('h9), .width(6)) MINUTES (
    .clr(RESET_out), .load(comparator_2_eq), .up(1'b0), .clk(not_1_out), .D(6'b001001), .Q(MINUTES_q));  // open: count, carry
  Counter #(.max('h4), .width(4)) PERIOD (
    .clr(RESET_out), .load(comparator_3_eq), .clk(not_2_out), .D(4'b0001), .Q(PERIOD_q));  // open: up, count, carry
  // _7_Segment_Display 7_segment_display_1: pin names not known; wires that end beside it: n7_segment_display_1_p1, n7_segment_display_1_p1
  // BCD_to_7_Segment_decoder bcd_to_7_segment_decoder_1: pin names not known
  // Binary_to_BCD_converter #(.binvalue(6)) binary_to_bcd_converter_1: pin names not known; wires that end beside it: SECONDS_q
  // _7_Segment_Display 7_segment_display_2: pin names not known; wires that end beside it: n7_segment_display_2_p1, n7_segment_display_2_p1
  // BCD_to_7_Segment_decoder bcd_to_7_segment_decoder_2: pin names not known
  // Binary_to_BCD_converter #(.binvalue(6)) binary_to_bcd_converter_2: pin names not known; wires that end beside it: MINUTES_q
  // Binary_to_BCD_converter #(.binvalue(4)) binary_to_bcd_converter_3: pin names not known; wires that end beside it: PERIOD_q, binary_to_bcd_converter_3_p2, binary_to_bcd_converter_3_p2
  // _7_Segment_Display 7_segment_display_3: pin names not known; wires that end beside it: n7_segment_display_3_p1, n7_segment_display_3_p1
  // BCD_to_7_Segment_decoder bcd_to_7_segment_decoder_3: pin names not known
  Comparator #(.width(6)) comparator_1 (.a(SECONDS_q), .b({6{1'b0}}), .eq(comparator_1_eq));  // open: gt, lt
  // _7_Segment_Display 7_segment_display_4: pin names not known; wires that end beside it: n7_segment_display_4_p1, n7_segment_display_4_p1
  // BCD_to_7_Segment_decoder bcd_to_7_segment_decoder_4: pin names not known
  Comparator #(.width(6)) comparator_2 (.a(MINUTES_q), .b({6{1'b0}}), .eq(comparator_2_eq));  // open: gt, lt
  // _7_Segment_Display 7_segment_display_5: pin names not known; wires that end beside it: n7_segment_display_5_p1, n7_segment_display_5_p1
  // BCD_to_7_Segment_decoder bcd_to_7_segment_decoder_5: pin names not known
  Comparator #(.width(4)) comparator_3 (.a(PERIOD_q), .b(4'b0000), .eq(comparator_3_eq));  // open: gt, lt
  and and_1 (and_1_out, comparator_1_eq, comparator_2_eq);
  // Buzzer buzzer_1: pin names not known; wires that end beside it: 7'b0110010, 14'h215, and_1_out
endmodule

module ATTACK_TIMER (
  input  in_1
);

  wire button_1_out, clock_1_out, comparator_1_eq, comparator_2_eq, n7_segment_display_1_p1,
       n7_segment_display_2_p1, not_1_out, t_ff_1_qn;
  wire [4:0] ATTACK_TIME_q;

  Button button_1 (.out(button_1_out));
  Clock clock_1 (.out(clock_1_out));
  Counter #(.max('h18), .width(5)) ATTACK_TIME (
    .clr(button_1_out), .up(in_1), .clk(clock_1_out), .D(5'b11000), .Q(ATTACK_TIME_q));  // open: load, count, carry
  LED led_1 (.in(t_ff_1_qn));
  // _7_Segment_Display 7_segment_display_1: pin names not known; wires that end beside it: n7_segment_display_1_p1, n7_segment_display_1_p1
  // BCD_to_7_Segment_decoder bcd_to_7_segment_decoder_1: pin names not known
  // Binary_to_BCD_converter #(.binvalue(5)) binary_to_bcd_converter_1: pin names not known; wires that end beside it: ATTACK_TIME_q
  // _7_Segment_Display 7_segment_display_2: pin names not known; wires that end beside it: n7_segment_display_2_p1, n7_segment_display_2_p1
  // BCD_to_7_Segment_decoder bcd_to_7_segment_decoder_2: pin names not known
  Comparator #(.width(5)) comparator_1 (.a({5{1'b0}}), .b(ATTACK_TIME_q), .eq(comparator_1_eq));  // open: gt, lt
  Comparator #(.width(5)) comparator_2 (.a(5'b00001), .b(ATTACK_TIME_q), .eq(comparator_2_eq));  // open: gt, lt
  T_Flip_Flop t_ff_1 (.T(1'b1), .clk(comparator_1_eq), .Qn(t_ff_1_qn));  // open: Q, reset, preset
  not not_1 (not_1_out, t_ff_1_qn);
  LED led_2 (.in(comparator_2_eq));
  // Buzzer buzzer_1: pin names not known; wires that end beside it: 14'h215, comparator_2_eq, 7'b0110010
  LED led_3 (.in(not_1_out));

  // Notes on the sheet:
  //   POSSESION
  //   POSSESION
endmodule

module FOULS (
);

  wire ADD_FOUL_out, binary_to_bcd_converter_1_p2, comparator_1_eq, RESET_FOULS_out;
  wire [3:0] adder_1_out, FOULS_q;

  Button RESET_FOULS (.out(RESET_FOULS_out));
  Button ADD_FOUL (.out(ADD_FOUL_out));
  Counter #(.max('h5), .width(4)) FOULS (
    .clr(RESET_FOULS_out), .load(1'b1), .up(1'b1), .clk(ADD_FOUL_out), .D(adder_1_out), .Q(FOULS_q));  // open: count, carry
  Adder #(.width(4)) adder_1 (.a(FOULS_q), .b(4'b0001), .out(adder_1_out));  // open: cin, cout
  // Binary_to_BCD_converter #(.binvalue(4)) binary_to_bcd_converter_1: pin names not known; wires that end beside it: FOULS_q, binary_to_bcd_converter_1_p2
  _7_Segment_Display u_7_segment_display_1 ();  // open: g, f, a, b, e, d, c, dp
  // BCD_to_7_Segment_decoder bcd_to_7_segment_decoder_1: pin names not known; wires that end beside it: binary_to_bcd_converter_1_p2
  Comparator #(.width(4)) comparator_1 (.a(FOULS_q), .b(4'b0101), .eq(comparator_1_eq));  // open: gt, lt
  LED led_1 (.in(comparator_1_eq));
endmodule

module PLUS123_1 (
  input  A,
  input  B,
  input  C,
  input  D,
  output [1:0] F1,
  output F2
);

  wire and_1_out, and_2_out, and_3_out, and_4_out, and_5_out, and_6_out, and_7_out, and_8_out, not_1_out,
       not_2_out, not_3_out, not_4_out;

  not not_1 (not_1_out, A);
  not not_2 (not_2_out, B);
  not not_3 (not_3_out, C);
  not not_4 (not_4_out, D);
  and and_1 (and_1_out, not_1_out, not_2_out, not_3_out, D);
  and and_2 (and_2_out, not_1_out, not_2_out, C, not_4_out);
  and and_3 (and_3_out, not_1_out, not_2_out, not_3_out, D);
  and and_4 (and_4_out, not_1_out, B, not_3_out, not_4_out);
  and and_5 (and_5_out, not_1_out, not_2_out, not_3_out, D);
  and and_6 (and_6_out, not_1_out, not_2_out, C, not_4_out);
  and and_7 (and_7_out, not_1_out, B, not_3_out, not_4_out);
  and and_8 (and_8_out, A, not_2_out, not_3_out, not_4_out);
  or or_1 (F1[1], and_1_out, and_2_out);
  or or_2 (F1[0], and_3_out, and_4_out);
  or or_3 (F2, and_5_out, and_6_out, and_7_out, and_8_out);
endmodule

module COUNTER123 (
);

  wire bcd_to_7_segment_decoder_3_p1, binary_to_bcd_converter_1_p2, binary_to_bcd_converter_1_p4,
       clock_1_out, MINUS1_out, PLUS1_out, PLUS2_out, PLUS3_out, plus123_1_1_f2, RESET_SCORE_out, switch_1_p2;
  wire [1:0] plus123_1_1_f1;
  wire [7:0] adder_1_out, multiplexer_1_out, negator_1_out, SCORE_q;

  Button PLUS1 (.out(PLUS1_out));
  Button PLUS2 (.out(PLUS2_out));
  Button PLUS3 (.out(PLUS3_out));
  Button MINUS1 (.out(MINUS1_out));
  Clock clock_1 (.out(clock_1_out));
  Negator negator_1 (.in(8'h1), .out(negator_1_out));
  // Switch switch_1: pin names not known; wires that end beside it: clock_1_out, switch_1_p2, 1'b1
  Multiplexer #(.enable("true"), .select(2), .width(8)) multiplexer_1 (
    .in0(8'h1), .in1(8'h2), .in2(8'h3), .in3(negator_1_out), .out(multiplexer_1_out), .sel(plus123_1_1_f1),
    .en(plus123_1_1_f2));
  Counter SCORE (
    .clr(RESET_SCORE_out), .load(1'b1), .up(1'b1), .clk(switch_1_p2), .D(adder_1_out), .Q(SCORE_q));  // open: count, carry
  Button RESET_SCORE (.out(RESET_SCORE_out));
  PLUS123_1 plus123_1_1 (
    .A(PLUS1_out), .B(PLUS2_out), .C(PLUS3_out), .D(MINUS1_out), .F1(plus123_1_1_f1), .F2(plus123_1_1_f2));
  _7_Segment_Display u_7_segment_display_1 ();  // open: g, f, a, b, e, d, c, dp
  // BCD_to_7_Segment_decoder bcd_to_7_segment_decoder_1: pin names not known
  // Binary_to_BCD_converter #(.binvalue(8)) binary_to_bcd_converter_1: pin names not known; wires that end beside it: SCORE_q, binary_to_bcd_converter_1_p2, binary_to_bcd_converter_1_p2, binary_to_bcd_converter_1_p4
  Adder adder_1 (.a(SCORE_q), .b(multiplexer_1_out), .out(adder_1_out));  // open: cin, cout
  _7_Segment_Display u_7_segment_display_2 ();  // open: g, f, a, b, e, d, c, dp
  _7_Segment_Display u_7_segment_display_3 ();  // open: g, f, a, b, e, d, c, dp
  // BCD_to_7_Segment_decoder bcd_to_7_segment_decoder_2: pin names not known; wires that end beside it: binary_to_bcd_converter_1_p4
  // BCD_to_7_Segment_decoder bcd_to_7_segment_decoder_3: pin names not known; wires that end beside it: bcd_to_7_segment_decoder_3_p1, bcd_to_7_segment_decoder_3_p1
endmodule
